# Fritzing sketch modele 1 (saved by Fritzing 0.9.2b)
circuit board: 15.1247cm x 26.8437cm
circuit board: 8.35731cm x 9.86456cm
breadboards: 1

parts:
  R1 = Resistor [tolerance=±5% resistance=220 package=THT]
  R2 = Resistor [tolerance=±5% resistance=220 package=THT]
  R3 = Resistor [tolerance=±5% resistance=220 package=THT]
  LED1 = LED - 5mm [color="Red (633nm)" package="5 mm [THT]"]
  LED2 = LED - 5mm [color="Red (633nm)" package="5 mm [THT]"]
  LED3 = LED - 5mm [color="Red (633nm)" package="5 mm [THT]"]
  LED4 = LED - 5mm [color="Red (633nm)" package="5 mm [THT]"]
  S1 = Round Pushbutton
  S2 = Round Pushbutton
  S3 = Round Pushbutton
  S4 = Round Pushbutton
  R4 = Resistor [tolerance=±5% resistance=220 package=THT]
  LED7 = LED - 5mm [color="Red (633nm)" package="5 mm [THT]"]
  LED8 = LED - 5mm [color="Red (633nm)" package="5 mm [THT]"]
  S7 = Round Pushbutton
  S8 = Round Pushbutton
  LED5 = LED - 5mm [color="Red (633nm)" package="5 mm [THT]"]
  LED6 = LED - 5mm [color="Red (633nm)" package="5 mm [THT]"]
  S6 = Round Pushbutton
  S5 = Round Pushbutton
  LED9 = LED - 5mm [color="Red (633nm)" package="5 mm [THT]"]
  LED10 = LED - 5mm [color="Red (633nm)" package="5 mm [THT]"]
  S9 = Round Pushbutton
  S10 = Round Pushbutton
  LED11 = LED - 5mm [color="Red (633nm)" package="5 mm [THT]"]
  LED12 = LED - 5mm [color="Red (633nm)" package="5 mm [THT]"]
  S11 = Round Pushbutton
  S12 = Round Pushbutton
  R5 = Resistor [tolerance=±5% resistance=220 package=THT]
  LED13 = LED - 5mm [color="Red (633nm)" package="5 mm [THT]"]
  LED14 = LED - 5mm [color="Red (633nm)" package="5 mm [THT]"]
  S13 = Round Pushbutton
  S14 = Round Pushbutton
  LED15 = LED - 5mm [color="Red (633nm)" package="5 mm [THT]"]
  LED16 = LED - 5mm [color="Red (633nm)" package="5 mm [THT]"]
  S15 = Round Pushbutton
  S16 = Round Pushbutton
  R6 = Resistor [tolerance=±5% resistance=220 package=THT]
  R7 = Resistor [tolerance=±5% resistance=220 package=THT]
  R8 = Resistor [tolerance=±5% resistance=220 package=THT]
  part = LED - 5mm [color="Red (633nm)" package="5 mm [THT]"]
  LED18 = LED - 5mm [color="Red (633nm)" package="5 mm [THT]"]
  S17 = Round Pushbutton
  S18 = Round Pushbutton
  LED19 = LED - 5mm [color="Red (633nm)" package="5 mm [THT]"]
  LED20 = LED - 5mm [color="Red (633nm)" package="5 mm [THT]"]
  S19 = Round Pushbutton
  S20 = Round Pushbutton
  LED21 = LED - 5mm [color="Red (633nm)" package="5 mm [THT]"]
  part_2 = LED - 5mm [color="Red (633nm)" package="5 mm [THT]"]
  S21 = Round Pushbutton
  S22 = Round Pushbutton
  R9 = Resistor [tolerance=±5% resistance=220 package=THT]
  LED22 = LED - 5mm [color="Red (633nm)" package="5 mm [THT]"]
  LED23 = LED - 5mm [color="Red (633nm)" package="5 mm [THT]"]
  S23 = Round Pushbutton
  S24 = Round Pushbutton
  LED24 = LED - 5mm [color="Red (633nm)" package="5 mm [THT]"]
  LED25 = LED - 5mm [color="Red (633nm)" package="5 mm [THT]"]
  S25 = Round Pushbutton
  S26 = Round Pushbutton
  LED27 = LED - 5mm [color="Red (633nm)" package="5 mm [THT]"]
  LED28 = LED - 5mm [color="Red (633nm)" package="5 mm [THT]"]
  S27 = Round Pushbutton
  S28 = Round Pushbutton
  R10 = Resistor [tolerance=±5% resistance=220 package=THT]
  S29 = Round Pushbutton
  LED31 = LED - 5mm [color="Red (633nm)" package="5 mm [THT]"]
  LED32 = LED - 5mm [color="Red (633nm)" package="5 mm [THT]"]
  S31 = Round Pushbutton
  S32 = Round Pushbutton
  LED33 = LED - 5mm [color="Red (633nm)" package="5 mm [THT]"]
  LED34 = LED - 5mm [color="Red (633nm)" package="5 mm [THT]"]
  S33 = Round Pushbutton
  S34 = Round Pushbutton
  LED35 = LED - 5mm [color="Red (633nm)" package="5 mm [THT]"]
  LED36 = LED - 5mm [color="Red (633nm)" package="5 mm [THT]"]
  S35 = Round Pushbutton
  S36 = Round Pushbutton
  R12 = Resistor [tolerance=±5% resistance=220 package=THT]
  LED37 = LED - 5mm [color="Red (633nm)" package="5 mm [THT]"]
  LED38 = LED - 5mm [color="Red (633nm)" package="5 mm [THT]"]
  S37 = Round Pushbutton
  S38 = Round Pushbutton
  LED39 = LED - 5mm [color="Red (633nm)" package="5 mm [THT]"]
  LED40 = LED - 5mm [color="Red (633nm)" package="5 mm [THT]"]
  S39 = Round Pushbutton
  S40 = Round Pushbutton
  LED41 = LED - 5mm [color="Red (633nm)" package="5 mm [THT]"]
  LED42 = LED - 5mm [color="Red (633nm)" package="5 mm [THT]"]
  S41 = Round Pushbutton
  S42 = Round Pushbutton
  LED45 = LED - 5mm [color="Red (633nm)" package="5 mm [THT]"]
  LED46 = LED - 5mm [color="Red (633nm)" package="5 mm [THT]"]
  S45 = Round Pushbutton
  S46 = Round Pushbutton
  R13 = Resistor [tolerance=±5% resistance=220 package=THT]
  LED47 = LED - 5mm [color="Red (633nm)" package="5 mm [THT]"]
  LED48 = LED - 5mm [color="Red (633nm)" package="5 mm [THT]"]
  S47 = Round Pushbutton
  S48 = Round Pushbutton
  LED49 = LED - 5mm [color="Red (633nm)" package="5 mm [THT]"]
  LED50 = LED - 5mm [color="Red (633nm)" package="5 mm [THT]"]
  S49 = Round Pushbutton
  S50 = Round Pushbutton
  LED30 = LED - 5mm [color="Red (633nm)" package="5 mm [THT]"]
  LED29 = LED - 5mm [color="Red (633nm)" package="5 mm [THT]"]
  S30 = Round Pushbutton

nets:
  N1: R1.Pin_0, LED1.anode, LED2.cathode, LED5.anode, LED6.cathode, LED15.anode, LED16.cathode
  N2: R2.Pin_0, LED3.anode, LED4.cathode, S1.leg1, S2.leg1, LED11.anode, LED12.cathode
  N3: R3.Pin_0, S3.leg1, S4.leg1, LED7.cathode, LED8.anode, S6.leg1, S5.leg1, LED9.cathode, LED10.anode
  N4: LED1.cathode, S1.leg0
  N5: LED2.anode, S2.leg0
  N6: LED3.cathode, S3.leg0
  N7: LED4.anode, S4.leg0
  N8: R4.Pin_0, S7.leg1, S8.leg1, S9.leg1, S10.leg1, S11.leg1, S12.leg1, LED13.anode, LED14.cathode
  N9: LED7.anode, S7.leg0
  N10: LED8.cathode, S8.leg0
  N11: LED5.cathode, S5.leg0
  N12: LED6.anode, S6.leg0
  N13: LED9.anode, S10.leg0
  N14: LED10.cathode, S9.leg0
  N15: LED11.cathode, S12.leg0
  N16: LED12.anode, S11.leg0
  N17: R5.Pin_0, S13.leg1, S14.leg1
  N18: LED13.cathode, S13.leg0
  N19: LED14.anode, S14.leg0
  N20: LED15.cathode, S16.leg0
  N21: LED16.anode, S15.leg0
  N22: S15.leg1, S16.leg1
  N23: R6.Pin_0, part.cathode, LED18.anode, LED21.cathode, part_2.anode, LED27.cathode, LED28.anode, LED35.anode, LED36.cathode, LED45.cathode, LED46.anode
  N24: R7.Pin_0, S17.leg1, S18.leg1, LED19.anode, LED20.cathode, LED24.anode, LED25.cathode, LED33.anode, LED34.cathode, LED49.cathode, LED50.anode
  N25: R8.Pin_0, S19.leg1, S20.leg1, S21.leg1, S22.leg1, LED22.cathode, LED23.anode, LED31.anode, LED32.cathode, LED41.cathode, LED42.anode
  N26: part.anode, S18.leg0
  N27: LED18.cathode, S17.leg0
  N28: LED19.cathode, S20.leg0
  N29: LED20.anode, S19.leg0
  N30: LED21.anode, S21.leg0
  N31: part_2.cathode, S22.leg0
  N32: R9.Pin_0, S23.leg1, S24.leg1, S25.leg1, S26.leg1, S27.leg1, S28.leg1, LED39.anode, LED40.cathode, LED30.cathode, LED29.anode
  N33: LED22.anode, S23.leg0
  N34: LED23.cathode, S24.leg0
  N35: LED24.cathode, S26.leg0
  N36: LED25.anode, S25.leg0
  N37: LED27.anode, S27.leg0
  N38: LED28.cathode, S28.leg0
  N39: R10.Pin_0, S29.leg1, S31.leg1, S32.leg1, S33.leg1, S34.leg1, S35.leg1, S36.leg1, LED37.anode, LED38.cathode, S30.leg1
  N40: S29.leg0, LED30.anode
  N41: LED31.cathode, S31.leg0
  N42: LED32.anode, S32.leg0
  N43: LED33.cathode, S33.leg0
  N44: LED34.anode, S34.leg0
  N45: LED35.cathode, S35.leg0
  N46: LED36.anode, S36.leg0
  N47: R12.Pin_0, S37.leg1, S38.leg1, S39.leg1, S40.leg1, S41.leg1, S42.leg1, S45.leg1, S46.leg1, LED47.anode, LED48.cathode
  N48: LED37.cathode, S37.leg0
  N49: LED38.anode, S38.leg0
  N50: LED39.cathode, S40.leg0
  N51: LED40.anode, S39.leg0
  N52: LED41.anode, S41.leg0
  N53: LED42.cathode, S42.leg0
  N54: LED45.anode, S46.leg0
  N55: LED46.cathode, S45.leg0
  N56: R13.Pin_0, S47.leg1, S48.leg1, S49.leg1, S50.leg1
  N57: LED47.cathode, S48.leg0
  N58: LED48.anode, S47.leg0
  N59: LED49.anode, S50.leg0
  N60: LED50.cathode, S49.leg0
  N61: LED29.cathode, S30.leg0
