# Fritzing sketch modele 2 (saved by Fritzing 0.9.2b)
circuit board: 10.9205cm x 9.04401cm
breadboards: 1

parts:
  S31 = Round Pushbutton
  R10 = Resistor [tolerance=±5% resistance=220 package=THT]
  S34 = Round Pushbutton
  LED32 = LED - 5mm [color="Red (633nm)" package="5 mm [THT]"]
  LED34 = LED - 5mm [color="Red (633nm)" package="5 mm [THT]"]
  LED33 = LED - 5mm [color="Red (633nm)" package="5 mm [THT]"]
  LED31 = LED - 5mm [color="Red (633nm)" package="5 mm [THT]"]
  S33 = Round Pushbutton
  R11 = Resistor [tolerance=±5% resistance=220 package=THT]
  S32 = Round Pushbutton
  LED35 = LED - 5mm [color="Red (633nm)" package="5 mm [THT]"]
  LED36 = LED - 5mm [color="Red (633nm)" package="5 mm [THT]"]
  S35 = Round Pushbutton
  S36 = Round Pushbutton
  R13 = Resistor [tolerance=±5% resistance=220 package=THT]
  R12 = Resistor [tolerance=±5% resistance=220 package=THT]
  LED37 = LED - 5mm [color="Red (633nm)" package="5 mm [THT]"]
  LED38 = LED - 5mm [color="Red (633nm)" package="5 mm [THT]"]
  S37 = Round Pushbutton
  S38 = Round Pushbutton
  LED39 = LED - 5mm [color="Red (633nm)" package="5 mm [THT]"]
  LED40 = LED - 5mm [color="Red (633nm)" package="5 mm [THT]"]
  S39 = Round Pushbutton
  S40 = Round Pushbutton
  LED41 = LED - 5mm [color="Red (633nm)" package="5 mm [THT]"]
  LED42 = LED - 5mm [color="Red (633nm)" package="5 mm [THT]"]
  S41 = Round Pushbutton
  S42 = Round Pushbutton
  R14 = Resistor [tolerance=±5% resistance=220 package=THT]
  LED43 = LED - 5mm [color="Red (633nm)" package="5 mm [THT]"]
  S43 = Round Pushbutton
  LED44 = LED - 5mm [color="Red (633nm)" package="5 mm [THT]"]
  S44 = Round Pushbutton
  LED45 = LED - 5mm [color="Red (633nm)" package="5 mm [THT]"]
  LED46 = LED - 5mm [color="Red (633nm)" package="5 mm [THT]"]
  S45 = Round Pushbutton
  S46 = Round Pushbutton
  LED47 = LED - 5mm [color="Red (633nm)" package="5 mm [THT]"]
  LED48 = LED - 5mm [color="Red (633nm)" package="5 mm [THT]"]
  S47 = Round Pushbutton
  S48 = Round Pushbutton
  LED49 = LED - 5mm [color="Red (633nm)" package="5 mm [THT]"]
  LED50 = LED - 5mm [color="Red (633nm)" package="5 mm [THT]"]
  S49 = Round Pushbutton
  S50 = Round Pushbutton

nets:
  N1: S31.leg0, LED31.anode
  N2: S31.leg1, S34.leg0, S33.leg0, R11.Pin_0, S32.leg1, S39.leg0, S40.leg0, S47.leg0, S48.leg0
  N3: R10.Pin_0, LED32.anode, LED31.cathode, LED35.cathode, LED36.anode, LED41.cathode, LED42.anode, LED49.cathode, LED50.anode
  N4: S34.leg1, LED34.anode
  N5: LED32.cathode, S32.leg0
  N6: LED34.cathode, LED33.anode, S35.leg1, S36.leg1, R12.Pin_0, LED37.cathode, LED38.anode, LED45.cathode, LED46.anode
  N7: LED33.cathode, S33.leg1
  N8: LED35.anode, S35.leg0
  N9: LED36.cathode, S36.leg0
  N10: R13.Pin_0, S37.leg1, S38.leg1, LED39.anode, LED40.cathode, S41.leg1, S42.leg1, S43.leg0, S44.leg0
  N11: LED37.anode, S37.leg0
  N12: LED38.cathode, S38.leg0
  N13: LED39.cathode, S39.leg1
  N14: LED40.anode, S40.leg1
  N15: LED41.anode, S41.leg0
  N16: LED42.cathode, S42.leg0
  N17: R14.Pin_0, LED43.anode, LED44.cathode, S45.leg1, S46.leg1, LED47.anode, LED48.cathode, S49.leg1, S50.leg1
  N18: LED43.cathode, S43.leg1
  N19: LED44.anode, S44.leg1
  N20: LED45.anode, S45.leg0
  N21: LED46.cathode, S46.leg0
  N22: LED47.cathode, S47.leg1
  N23: LED48.anode, S48.leg1
  N24: LED49.anode, S49.leg0
  N25: LED50.cathode, S50.leg0
