# Fritzing sketch modele 4 (saved by Fritzing 0.9.2b)
circuit board: 19.8552cm x 27.3308cm
breadboards: 1

parts:
  R01 = Resistor [tolerance=±5% resistance=220 package=THT]
  R02 = Resistor [tolerance=±5% resistance=220 package=THT]
  LED2 = LED - 5mm [color="Red (633nm)" package="5 mm [THT]"]
  S2 = Square Pushbutton
  LED3 = LED - 5mm [color="Red (633nm)" package="5 mm [THT]"]
  S3 = Square Pushbutton
  LED4 = LED - 5mm [color="Red (633nm)" package="5 mm [THT]"]
  S5 = Square Pushbutton
  LED5 = LED - 5mm [color="Red (633nm)" package="5 mm [THT]"]
  S4 = Square Pushbutton
  R03 = Resistor [tolerance=±5% resistance=220 package=THT]
  LED6 = LED - 5mm [color="Red (633nm)" package="5 mm [THT]"]
  S6 = Square Pushbutton
  LED7 = LED - 5mm [color="Red (633nm)" package="5 mm [THT]"]
  S7 = Square Pushbutton
  R04 = Resistor [tolerance=±5% resistance=220 package=THT]
  LED8 = LED - 5mm [color="Red (633nm)" package="5 mm [THT]"]
  S8 = Square Pushbutton
  LED9 = LED - 5mm [color="Red (633nm)" package="5 mm [THT]"]
  S9 = Square Pushbutton
  LED10 = LED - 5mm [color="Red (633nm)" package="5 mm [THT]"]
  S10 = Square Pushbutton
  LED11 = LED - 5mm [color="Red (633nm)" package="5 mm [THT]"]
  S11 = Square Pushbutton
  LED12 = LED - 5mm [color="Red (633nm)" package="5 mm [THT]"]
  S12 = Square Pushbutton
  LED13 = LED - 5mm [color="Red (633nm)" package="5 mm [THT]"]
  S13 = Square Pushbutton
  R05 = Resistor [tolerance=±5% resistance=220 package=THT]
  LED14 = LED - 5mm [color="Red (633nm)" package="5 mm [THT]"]
  LED15 = LED - 5mm [color="Red (633nm)" package="5 mm [THT]"]
  LED16 = LED - 5mm [color="Red (633nm)" package="5 mm [THT]"]
  S14 = Square Pushbutton
  S15 = Square Pushbutton
  S16 = Square Pushbutton
  LED17 = LED - 5mm [color="Red (633nm)" package="5 mm [THT]"]
  S17 = Square Pushbutton
  LED18 = LED - 5mm [color="Red (633nm)" package="5 mm [THT]"]
  LED19 = LED - 5mm [color="Red (633nm)" package="5 mm [THT]"]
  LED21 = LED - 5mm [color="Red (633nm)" package="5 mm [THT]"]
  S18 = Square Pushbutton
  S19 = Square Pushbutton
  S20 = Square Pushbutton
  S21 = Square Pushbutton
  LED22 = LED - 5mm [color="Red (633nm)" package="5 mm [THT]"]
  R06 = Resistor [tolerance=±5% resistance=220 package=THT]
  LED23 = LED - 5mm [color="Red (633nm)" package="5 mm [THT]"]
  LED24 = LED - 5mm [color="Red (633nm)" package="5 mm [THT]"]
  LED25 = LED - 5mm [color="Red (633nm)" package="5 mm [THT]"]
  LED26 = LED - 5mm [color="Red (633nm)" package="5 mm [THT]"]
  S22 = Square Pushbutton
  S23 = Square Pushbutton
  S24 = Square Pushbutton
  S25 = Square Pushbutton
  LED27 = LED - 5mm [color="Red (633nm)" package="5 mm [THT]"]
  S26 = Square Pushbutton
  LED28 = LED - 5mm [color="Red (660nm)" package="5 mm [THT]"]
  LED29 = LED - 5mm [color="Red (633nm)" package="5 mm [THT]"]
  LED30 = LED - 5mm [color="Red (633nm)" package="5 mm [THT]"]
  LED31 = LED - 5mm [color="Red (633nm)" package="5 mm [THT]"]
  S27 = Square Pushbutton
  S28 = Square Pushbutton
  S29 = Square Pushbutton
  S30 = Square Pushbutton
  LED32 = LED - 5mm [color="Red (633nm)" package="5 mm [THT]"]
  S31 = Square Pushbutton
  R07 = Resistor [tolerance=±5% resistance=220 package=THT]
  LED33 = LED - 5mm [color="Red (633nm)" package="5 mm [THT]"]
  LED34 = LED - 5mm [color="Red (633nm)" package="5 mm [THT]"]
  LED35 = LED - 5mm [color="Red (633nm)" package="5 mm [THT]"]
  LED36 = LED - 5mm [color="Red (633nm)" package="5 mm [THT]"]
  LED37 = LED - 5mm [color="Red (633nm)" package="5 mm [THT]"]
  S32 = Square Pushbutton
  S33 = Square Pushbutton
  S34 = Square Pushbutton
  S35 = Square Pushbutton
  S36 = Square Pushbutton
  LED38 = LED - 5mm [color="Red (633nm)" package="5 mm [THT]"]
  S37 = Square Pushbutton
  LED39 = LED - 5mm [color="Red (633nm)" package="5 mm [THT]"]
  LED40 = LED - 5mm [color="Red (633nm)" package="5 mm [THT]"]
  LED41 = LED - 5mm [color="Red (633nm)" package="5 mm [THT]"]
  LED42 = LED - 5mm [color="Red (633nm)" package="5 mm [THT]"]
  LED43 = LED - 5mm [color="Red (633nm)" package="5 mm [THT]"]
  S38 = Square Pushbutton
  S39 = Square Pushbutton
  S40 = Square Pushbutton
  S41 = Square Pushbutton
  S42 = Square Pushbutton
  LED44 = LED - 5mm [color="Red (633nm)" package="5 mm [THT]"]
  S43 = Square Pushbutton
  R08 = Resistor [tolerance=±5% resistance=220 package=THT]
  LED45 = LED - 5mm [color="Red (633nm)" package="5 mm [THT]"]
  LED46 = LED - 5mm [color="Red (633nm)" package="5 mm [THT]"]
  LED47 = LED - 5mm [color="Red (633nm)" package="5 mm [THT]"]
  LED48 = LED - 5mm [color="Red (633nm)" package="5 mm [THT]"]
  LED49 = LED - 5mm [color="Red (633nm)" package="5 mm [THT]"]
  LED50 = LED - 5mm [color="Red (633nm)" package="5 mm [THT]"]
  S44 = Square Pushbutton
  S45 = Square Pushbutton
  S46 = Square Pushbutton
  S47 = Square Pushbutton
  S48 = Square Pushbutton
  S49 = Square Pushbutton
  LED51 = LED - 5mm [color="Red (633nm)" package="5 mm [THT]"]
  S50 = Square Pushbutton
  LED52 = LED - 5mm [color="Red (633nm)" package="5 mm [THT]"]
  LED53 = LED - 5mm [color="Red (633nm)" package="5 mm [THT]"]
  LED54 = LED - 5mm [color="Red (633nm)" package="5 mm [THT]"]
  LED55 = LED - 5mm [color="Red (633nm)" package="5 mm [THT]"]
  LED56 = LED - 5mm [color="Red (633nm)" package="5 mm [THT]"]
  LED57 = LED - 5mm [color="Red (633nm)" package="5 mm [THT]"]
  S51 = Square Pushbutton
  S52 = Square Pushbutton
  S53 = Square Pushbutton
  S54 = Square Pushbutton
  S55 = Square Pushbutton
  S56 = Square Pushbutton
  LED58 = LED - 5mm [color="Red (633nm)" package="5 mm [THT]"]
  S57 = Square Pushbutton
  R09 = Resistor [tolerance=±5% resistance=220 package=THT]
  LED59 = LED - 5mm [color="Red (633nm)" package="5 mm [THT]"]
  LED60 = LED - 5mm [color="Red (633nm)" package="5 mm [THT]"]
  LED61 = LED - 5mm [color="Red (633nm)" package="5 mm [THT]"]
  LED62 = LED - 5mm [color="Red (633nm)" package="5 mm [THT]"]
  LED63 = LED - 5mm [color="Red (633nm)" package="5 mm [THT]"]
  LED64 = LED - 5mm [color="Red (633nm)" package="5 mm [THT]"]
  LED65 = LED - 5mm [color="Red (633nm)" package="5 mm [THT]"]
  S58 = Square Pushbutton
  S59 = Square Pushbutton
  S60 = Square Pushbutton
  S61 = Square Pushbutton
  S62 = Square Pushbutton
  S63 = Square Pushbutton
  S64 = Square Pushbutton
  LED66 = LED - 5mm [color="Red (633nm)" package="5 mm [THT]"]
  S65 = Square Pushbutton
  LED67 = LED - 5mm [color="Red (633nm)" package="5 mm [THT]"]
  LED68 = LED - 5mm [color="Red (633nm)" package="5 mm [THT]"]
  LED69 = LED - 5mm [color="Red (633nm)" package="5 mm [THT]"]
  LED70 = LED - 5mm [color="Red (633nm)" package="5 mm [THT]"]
  LED71 = LED - 5mm [color="Red (633nm)" package="5 mm [THT]"]
  LED72 = LED - 5mm [color="Red (633nm)" package="5 mm [THT]"]
  LED73 = LED - 5mm [color="Red (633nm)" package="5 mm [THT]"]
  S66 = Square Pushbutton
  S67 = Square Pushbutton
  S68 = Square Pushbutton
  S69 = Square Pushbutton
  S70 = Square Pushbutton
  S71 = Square Pushbutton
  S72 = Square Pushbutton
  LED75 = LED - 5mm [color="Red (633nm)" package="5 mm [THT]"]
  S74 = Square Pushbutton
  R10 = Resistor [tolerance=±5% resistance=220 package=THT]
  LED76 = LED - 5mm [color="Red (633nm)" package="5 mm [THT]"]
  LED77 = LED - 5mm [color="Red (633nm)" package="5 mm [THT]"]
  LED78 = LED - 5mm [color="Red (633nm)" package="5 mm [THT]"]
  LED79 = LED - 5mm [color="Red (633nm)" package="5 mm [THT]"]
  LED80 = LED - 5mm [color="Red (633nm)" package="5 mm [THT]"]
  LED81 = LED - 5mm [color="Red (633nm)" package="5 mm [THT]"]
  LED82 = LED - 5mm [color="Red (633nm)" package="5 mm [THT]"]
  LED83 = LED - 5mm [color="Red (633nm)" package="5 mm [THT]"]
  S75 = Square Pushbutton
  S76 = Square Pushbutton
  S77 = Square Pushbutton
  S78 = Square Pushbutton
  S79 = Square Pushbutton
  S80 = Square Pushbutton
  S81 = Square Pushbutton
  S82 = Square Pushbutton
  LED84 = LED - 5mm [color="Red (633nm)" package="5 mm [THT]"]
  LED85 = LED - 5mm [color="Red (633nm)" package="5 mm [THT]"]
  LED86 = LED - 5mm [color="Red (633nm)" package="5 mm [THT]"]
  LED87 = LED - 5mm [color="Red (633nm)" package="5 mm [THT]"]
  LED88 = LED - 5mm [color="Red (633nm)" package="5 mm [THT]"]
  LED89 = LED - 5mm [color="Red (633nm)" package="5 mm [THT]"]
  LED90 = LED - 5mm [color="Red (633nm)" package="5 mm [THT]"]
  LED91 = LED - 5mm [color="Red (633nm)" package="5 mm [THT]"]
  S83 = Square Pushbutton
  S84 = Square Pushbutton
  S85 = Square Pushbutton
  S86 = Square Pushbutton
  S87 = Square Pushbutton
  S88 = Square Pushbutton
  S89 = Square Pushbutton
  S90 = Square Pushbutton
  LED92 = LED - 5mm [color="Red (633nm)" package="5 mm [THT]"]
  S91 = Square Pushbutton
  LED93 = LED - 5mm [color="Red (633nm)" package="5 mm [THT]"]
  S92 = Square Pushbutton
  R11 = Resistor [tolerance=±5% resistance=220 package=THT]
  LED94 = LED - 5mm [color="Red (633nm)" package="5 mm [THT]"]
  LED95 = LED - 5mm [color="Red (633nm)" package="5 mm [THT]"]
  LED96 = LED - 5mm [color="Red (633nm)" package="5 mm [THT]"]
  LED97 = LED - 5mm [color="Red (633nm)" package="5 mm [THT]"]
  LED98 = LED - 5mm [color="Red (633nm)" package="5 mm [THT]"]
  LED99 = LED - 5mm [color="Red (633nm)" package="5 mm [THT]"]
  LED100 = LED - 5mm [color="Red (633nm)" package="5 mm [THT]"]
  LED101 = LED - 5mm [color="Red (633nm)" package="5 mm [THT]"]
  LED102 = LED - 5mm [color="Red (633nm)" package="5 mm [THT]"]
  S93 = Square Pushbutton
  S94 = Square Pushbutton
  S95 = Square Pushbutton
  S96 = Square Pushbutton
  S97 = Square Pushbutton
  S98 = Square Pushbutton
  S99 = Square Pushbutton
  S100 = Square Pushbutton
  S101 = Square Pushbutton
  LED103 = LED - 5mm [color="Red (633nm)" package="5 mm [THT]"]
  S102 = Square Pushbutton
  LED104 = LED - 5mm [color="Red (633nm)" package="5 mm [THT]"]
  LED105 = LED - 5mm [color="Red (633nm)" package="5 mm [THT]"]
  LED106 = LED - 5mm [color="Red (633nm)" package="5 mm [THT]"]
  LED107 = LED - 5mm [color="Red (633nm)" package="5 mm [THT]"]
  LED108 = LED - 5mm [color="Red (633nm)" package="5 mm [THT]"]
  LED109 = LED - 5mm [color="Red (633nm)" package="5 mm [THT]"]
  LED110 = LED - 5mm [color="Red (633nm)" package="5 mm [THT]"]
  LED111 = LED - 5mm [color="Red (633nm)" package="5 mm [THT]"]
  LED112 = LED - 5mm [color="Red (633nm)" package="5 mm [THT]"]
  S103 = Square Pushbutton
  S104 = Square Pushbutton
  S105 = Square Pushbutton
  S106 = Square Pushbutton
  S107 = Square Pushbutton
  S108 = Square Pushbutton
  S109 = Square Pushbutton
  S110 = Square Pushbutton
  S111 = Square Pushbutton
  S112 = Square Pushbutton
  R12 = Resistor [tolerance=±5% resistance=220 package=THT]
  LED114 = LED - 5mm [color="Red (633nm)" package="5 mm [THT]"]
  LED115 = LED - 5mm [color="Red (633nm)" package="5 mm [THT]"]
  LED116 = LED - 5mm [color="Red (633nm)" package="5 mm [THT]"]
  LED117 = LED - 5mm [color="Red (633nm)" package="5 mm [THT]"]
  LED118 = LED - 5mm [color="Red (633nm)" package="5 mm [THT]"]
  LED119 = LED - 5mm [color="Red (633nm)" package="5 mm [THT]"]
  LED120 = LED - 5mm [color="Red (633nm)" package="5 mm [THT]"]
  LED121 = LED - 5mm [color="Red (633nm)" package="5 mm [THT]"]
  LED122 = LED - 5mm [color="Red (633nm)" package="5 mm [THT]"]
  LED123 = LED - 5mm [color="Red (633nm)" package="5 mm [THT]"]
  S113 = Square Pushbutton
  S114 = Square Pushbutton
  S115 = Square Pushbutton
  S116 = Square Pushbutton
  S117 = Square Pushbutton
  S118 = Square Pushbutton
  S119 = Square Pushbutton
  S120 = Square Pushbutton
  S121 = Square Pushbutton
  S122 = Square Pushbutton
  R13 = Resistor [tolerance=±5% resistance=220 package=THT]
  LED124 = LED - 5mm [color="Red (633nm)" package="5 mm [THT]"]
  LED125 = LED - 5mm [color="Red (633nm)" package="5 mm [THT]"]
  LED126 = LED - 5mm [color="Red (633nm)" package="5 mm [THT]"]
  LED127 = LED - 5mm [color="Red (633nm)" package="5 mm [THT]"]
  LED128 = LED - 5mm [color="Red (633nm)" package="5 mm [THT]"]
  LED129 = LED - 5mm [color="Red (633nm)" package="5 mm [THT]"]
  LED130 = LED - 5mm [color="Red (633nm)" package="5 mm [THT]"]
  LED131 = LED - 5mm [color="Red (633nm)" package="5 mm [THT]"]
  LED132 = LED - 5mm [color="Red (633nm)" package="5 mm [THT]"]
  LED133 = LED - 5mm [color="Red (633nm)" package="5 mm [THT]"]
  S123 = Square Pushbutton
  S124 = Square Pushbutton
  S125 = Square Pushbutton
  S126 = Square Pushbutton
  S127 = Square Pushbutton
  S128 = Square Pushbutton
  S129 = Square Pushbutton
  S130 = Square Pushbutton
  S131 = Square Pushbutton
  S132 = Square Pushbutton
  R14 = Resistor [tolerance=±5% resistance=220 package=THT]
  LED134 = LED - 5mm [color="Red (633nm)" package="5 mm [THT]"]
  LED135 = LED - 5mm [color="Red (633nm)" package="5 mm [THT]"]
  LED136 = LED - 5mm [color="Red (633nm)" package="5 mm [THT]"]
  LED137 = LED - 5mm [color="Red (633nm)" package="5 mm [THT]"]
  LED138 = LED - 5mm [color="Red (633nm)" package="5 mm [THT]"]
  LED139 = LED - 5mm [color="Red (633nm)" package="5 mm [THT]"]
  LED140 = LED - 5mm [color="Red (633nm)" package="5 mm [THT]"]
  LED141 = LED - 5mm [color="Red (633nm)" package="5 mm [THT]"]
  LED142 = LED - 5mm [color="Red (633nm)" package="5 mm [THT]"]
  LED143 = LED - 5mm [color="Red (633nm)" package="5 mm [THT]"]
  S133 = Square Pushbutton
  S134 = Square Pushbutton
  S135 = Square Pushbutton
  S136 = Square Pushbutton
  S137 = Square Pushbutton
  S138 = Square Pushbutton
  S139 = Square Pushbutton
  S140 = Square Pushbutton
  S141 = Square Pushbutton
  S142 = Square Pushbutton
  LED144 = LED - 5mm [color="Red (633nm)" package="5 mm [THT]"]
  LED145 = LED - 5mm [color="Red (633nm)" package="5 mm [THT]"]
  LED146 = LED - 5mm [color="Red (633nm)" package="5 mm [THT]"]
  LED147 = LED - 5mm [color="Red (633nm)" package="5 mm [THT]"]
  LED148 = LED - 5mm [color="Red (633nm)" package="5 mm [THT]"]
  LED149 = LED - 5mm [color="Red (633nm)" package="5 mm [THT]"]
  LED150 = LED - 5mm [color="Red (633nm)" package="5 mm [THT]"]
  LED151 = LED - 5mm [color="Red (633nm)" package="5 mm [THT]"]
  LED152 = LED - 5mm [color="Red (633nm)" package="5 mm [THT]"]
  S143 = Square Pushbutton
  S144 = Square Pushbutton
  S145 = Square Pushbutton
  S146 = Square Pushbutton
  S147 = Square Pushbutton
  S148 = Square Pushbutton
  S149 = Square Pushbutton
  S150 = Square Pushbutton
  S151 = Square Pushbutton
  S152 = Square Pushbutton
  LED154 = LED - 5mm [color="Red (633nm)" package="5 mm [THT]"]
  LED155 = LED - 5mm [color="Red (633nm)" package="5 mm [THT]"]
  LED156 = LED - 5mm [color="Red (633nm)" package="5 mm [THT]"]
  LED157 = LED - 5mm [color="Red (633nm)" package="5 mm [THT]"]
  LED158 = LED - 5mm [color="Red (633nm)" package="5 mm [THT]"]
  LED159 = LED - 5mm [color="Red (633nm)" package="5 mm [THT]"]
  LED160 = LED - 5mm [color="Red (633nm)" package="5 mm [THT]"]
  LED161 = LED - 5mm [color="Red (633nm)" package="5 mm [THT]"]
  LED162 = LED - 5mm [color="Red (633nm)" package="5 mm [THT]"]
  S153 = Square Pushbutton
  S154 = Square Pushbutton
  S155 = Square Pushbutton
  S156 = Square Pushbutton
  S157 = Square Pushbutton
  S158 = Square Pushbutton
  S159 = Square Pushbutton
  S160 = Square Pushbutton
  S161 = Square Pushbutton
  S162 = Square Pushbutton
  LED164 = LED - 5mm [color="Red (633nm)" package="5 mm [THT]"]
  LED165 = LED - 5mm [color="Red (633nm)" package="5 mm [THT]"]
  LED166 = LED - 5mm [color="Red (633nm)" package="5 mm [THT]"]
  LED167 = LED - 5mm [color="Red (633nm)" package="5 mm [THT]"]
  LED168 = LED - 5mm [color="Red (633nm)" package="5 mm [THT]"]
  LED169 = LED - 5mm [color="Red (633nm)" package="5 mm [THT]"]
  LED170 = LED - 5mm [color="Red (633nm)" package="5 mm [THT]"]
  LED171 = LED - 5mm [color="Red (633nm)" package="5 mm [THT]"]
  LED172 = LED - 5mm [color="Red (633nm)" package="5 mm [THT]"]
  S163 = Square Pushbutton
  S164 = Square Pushbutton
  S165 = Square Pushbutton
  S166 = Square Pushbutton
  S167 = Square Pushbutton
  S168 = Square Pushbutton
  S169 = Square Pushbutton
  S170 = Square Pushbutton
  S171 = Square Pushbutton
  S172 = Square Pushbutton
  S173 = Square Pushbutton
  LED173 = LED - 5mm [color="Red (633nm)" package="5 mm [THT]"]
  LED174 = LED - 5mm [color="Red (633nm)" package="5 mm [THT]"]
  LED175 = LED - 5mm [color="Red (633nm)" package="5 mm [THT]"]
  LED176 = LED - 5mm [color="Red (633nm)" package="5 mm [THT]"]
  LED177 = LED - 5mm [color="Red (633nm)" package="5 mm [THT]"]
  LED178 = LED - 5mm [color="Red (633nm)" package="5 mm [THT]"]
  LED179 = LED - 5mm [color="Red (633nm)" package="5 mm [THT]"]
  S174 = Square Pushbutton
  S175 = Square Pushbutton
  LED180 = LED - 5mm [color="Red (633nm)" package="5 mm [THT]"]
  S176 = Square Pushbutton
  LED181 = LED - 5mm [color="Red (633nm)" package="5 mm [THT]"]
  S177 = Square Pushbutton
  LED182 = LED - 5mm [color="Red (633nm)" package="5 mm [THT]"]
  LED183 = LED - 5mm [color="Red (633nm)" package="5 mm [THT]"]
  S178 = Square Pushbutton
  S179 = Square Pushbutton
  LED184 = LED - 5mm [color="Red (633nm)" package="5 mm [THT]"]
  LED185 = LED - 5mm [color="Red (633nm)" package="5 mm [THT]"]
  S180 = Square Pushbutton
  S181 = Square Pushbutton
  LED186 = LED - 5mm [color="Red (633nm)" package="5 mm [THT]"]
  S182 = Square Pushbutton
  LED187 = LED - 5mm [color="Red (633nm)" package="5 mm [THT]"]
  S183 = Square Pushbutton
  LED188 = LED - 5mm [color="Red (633nm)" package="5 mm [THT]"]
  S184 = Square Pushbutton
  Composant1 = Arduino Mega 2560 (Rev3)
  U2 = MIDI_CONN_FEMALE [package=din_5_female]
  R15 = Resistor [tolerance=±5% resistance=220 package=THT]
  R16 = Resistor [tolerance=±5% resistance=220 package=THT]
  J3 = Power Jack [package=power_jack_pth_lock]

nets:
  N1: R01.Pin_0, LED2.cathode, LED3.cathode, S4.leg0, S6.leg0, LED8.cathode, S11.leg0, LED16.cathode, S20.leg0, LED25.cathode, S29.leg0, LED33.cathode, S41.leg0, LED48.cathode, S51.leg0, LED62.cathode, S72.leg0, LED80.cathode, S90.leg0, LED99.cathode, S111.leg0, LED120.cathode, LED130.cathode, LED140.cathode, S151.leg0, S161.leg0, S171.leg0
  N2: R01.Pin_1, Composant1.D12_PWM
  N3: R02.Pin_0, S2.leg0, LED4.cathode, LED5.anode, S7.leg0, LED9.cathode, S12.leg0, LED15.cathode, S18.leg0, LED24.cathode, S28.leg0, LED37.cathode, S39.leg0, LED49.cathode, S54.leg0, LED61.cathode, S69.leg0, LED79.cathode, S87.leg0, LED98.cathode, S108.leg0, LED119.cathode, LED129.cathode, LED139.cathode, S148.leg0, S158.leg0, S168.leg0
  N4: R02.Pin_1, Composant1.D11_PWM
  N5: LED2.anode, S2.leg1
  N6: LED3.anode, S3.leg1
  N7: S3.leg0, S5.leg0, R03.Pin_0, LED6.anode, LED7.anode, LED10.cathode, S13.leg0, LED14.cathode, S19.leg0, LED26.cathode, S27.leg0, LED36.cathode, S42.leg0, LED46.cathode, S55.leg0, LED64.cathode, S68.leg0, LED82.cathode, S86.leg0, LED101.cathode, S107.leg0, LED122.cathode, LED132.cathode, LED142.cathode, S147.leg0, S157.leg0, S167.leg0
  N8: LED4.anode, S5.leg1
  N9: LED5.cathode, S4.leg1
  N10: R03.Pin_1, Composant1.D10_PWM
  N11: LED6.cathode, S6.leg1
  N12: LED7.cathode, S7.leg1
  N13: R04.Pin_0, S8.leg0, S9.leg0, S10.leg0, LED11.anode, LED12.anode, LED13.anode, LED17.cathode, S21.leg0, LED23.cathode, S30.leg0, LED34.cathode, S38.leg0, LED50.cathode, S53.leg0, LED60.cathode, S70.leg0, LED78.cathode, S88.leg0, LED97.cathode, S109.leg0, LED118.cathode, LED128.cathode, LED138.cathode, S149.leg0, S159.leg0, S169.leg0
  N14: R04.Pin_1, Composant1.D9_PWM
  N15: LED8.anode, S8.leg1
  N16: LED9.anode, S9.leg1
  N17: LED10.anode, S10.leg1
  N18: LED11.cathode, S11.leg1
  N19: LED12.cathode, S12.leg1
  N20: LED13.cathode, S13.leg1
  N21: R05.Pin_0, S14.leg0, S15.leg0, S16.leg0, S17.leg0, LED18.anode, LED19.anode, LED21.anode, LED22.anode, LED27.cathode, S31.leg0, LED35.cathode, S40.leg0, LED45.cathode, S52.leg0, LED65.cathode, S71.leg0, LED83.cathode, S89.leg0, LED102.cathode, S110.leg0, LED123.cathode, LED133.cathode, LED143.cathode, S150.leg0, S160.leg0, S170.leg0
  N22: R05.Pin_1, Composant1.D8_PWM
  N23: LED14.anode, S14.leg1
  N24: LED15.anode, S15.leg1
  N25: LED16.anode, S16.leg1
  N26: LED17.anode, S17.leg1
  N27: LED18.cathode, S20.leg1
  N28: LED19.cathode, S18.leg1
  N29: LED21.cathode, S19.leg1
  N30: S21.leg1, LED22.cathode
  N31: R06.Pin_0, S22.leg0, S23.leg0, S24.leg0, S25.leg0, S26.leg0, LED28.anode, LED29.anode, LED30.anode, LED31.anode, LED32.anode, LED38.cathode, S43.leg0, LED47.cathode, S56.leg0, LED63.cathode, S67.leg0, LED81.cathode, S85.leg0, LED100.cathode, S106.leg0, LED121.cathode, LED131.cathode, LED141.cathode, S146.leg0, S156.leg0, S166.leg0
  N32: R06.Pin_1, Composant1.D7_PWM
  N33: LED23.anode, S23.leg1
  N34: LED24.anode, S25.leg1
  N35: LED25.anode, S24.leg1
  N36: LED26.anode, S22.leg1
  N37: LED27.anode, S26.leg1
  N38: LED28.cathode, S28.leg1
  N39: LED29.cathode, S30.leg1
  N40: LED30.cathode, S29.leg1
  N41: LED31.cathode, S27.leg1
  N42: LED32.cathode, S31.leg1
  N43: R07.Pin_0, S32.leg0, S33.leg0, S34.leg0, S35.leg0, S36.leg0, S37.leg0, LED39.anode, LED40.anode, LED41.anode, LED42.anode, LED43.anode, LED44.anode, LED51.cathode, S57.leg0, LED59.cathode, S66.leg0, LED77.cathode, S83.leg0, LED94.cathode, S105.leg0, LED114.cathode, LED124.cathode, LED134.cathode, S145.leg0, S155.leg0, S165.leg0
  N44: R07.Pin_1, Composant1.D6_PWM
  N45: LED33.anode, S35.leg1
  N46: LED34.anode, S34.leg1
  N47: LED35.anode, S32.leg1
  N48: LED36.anode, S33.leg1
  N49: LED37.anode, S36.leg1
  N50: LED38.anode, S37.leg1
  N51: LED39.cathode, S41.leg1
  N52: LED40.cathode, S40.leg1
  N53: LED41.cathode, S39.leg1
  N54: LED42.cathode, S38.leg1
  N55: LED43.cathode, S42.leg1
  N56: LED44.cathode, S43.leg1
  N57: R08.Pin_0, S44.leg0, S45.leg0, S46.leg0, S47.leg0, S48.leg0, S49.leg0, S50.leg0, LED52.anode, LED53.anode, LED54.anode, LED55.anode, LED56.anode, LED57.anode, LED58.anode, LED66.cathode, S74.leg0, LED76.cathode, S84.leg0, LED95.cathode, S104.leg0, LED117.cathode, LED127.cathode, LED137.cathode, S144.leg0, S154.leg0, S164.leg0
  N58: R08.Pin_1, Composant1.D5_PWM
  N59: LED45.anode, S44.leg1
  N60: LED46.anode, S45.leg1
  N61: LED47.anode, S48.leg1
  N62: LED48.anode, S49.leg1
  N63: LED49.anode, S47.leg1
  N64: LED50.anode, S46.leg1
  N65: LED51.anode, S50.leg1
  N66: LED52.cathode, S53.leg1
  N67: LED53.cathode, S54.leg1
  N68: LED54.cathode, S51.leg1
  N69: LED55.cathode, S52.leg1
  N70: LED56.cathode, S55.leg1
  N71: LED57.cathode, S56.leg1
  N72: LED58.cathode, S57.leg1
  N73: R09.Pin_0, S58.leg0, S59.leg0, S60.leg0, S61.leg0, S62.leg0, S63.leg0, S64.leg0, S65.leg0, LED67.anode, LED68.anode, LED69.anode, LED70.anode, LED71.anode, LED72.anode, LED73.anode, LED75.anode, S91.leg0, LED93.cathode, LED96.cathode, S103.leg0, LED115.cathode, LED125.cathode, LED135.cathode, S143.leg0, S153.leg0, S163.leg0
  N74: R09.Pin_1, Composant1.D4_PWM
  N75: LED59.anode, S58.leg1
  N76: LED60.anode, S62.leg1
  N77: LED61.anode, S61.leg1
  N78: LED62.anode, S59.leg1
  N79: LED63.anode, S60.leg1
  N80: LED64.anode, S63.leg1
  N81: LED65.anode, S64.leg1
  N82: LED66.anode, S65.leg1
  N83: LED67.cathode, S66.leg1
  N84: LED68.cathode, S67.leg1
  N85: LED69.cathode, S68.leg1
  N86: LED70.cathode, S71.leg1
  N87: LED71.cathode, S72.leg1
  N88: LED72.cathode, S69.leg1
  N89: LED73.cathode, S70.leg1
  N90: LED75.cathode, S74.leg1
  N91: R10.Pin_0, S75.leg0, S76.leg0, S77.leg0, S78.leg0, S79.leg0, S80.leg0, S81.leg0, S82.leg0, LED84.anode, LED85.anode, LED86.anode, LED87.anode, LED88.anode, LED89.anode, LED90.anode, LED91.anode, LED92.anode, S92.leg0, LED103.cathode, S112.leg0, LED116.cathode, LED126.cathode, LED136.cathode, S152.leg0, S162.leg0, S172.leg0
  N92: R10.Pin_1, Composant1.D3_PWM
  N93: LED76.anode, S75.leg1
  N94: LED77.anode, S76.leg1
  N95: LED78.anode, S80.leg1
  N96: LED79.anode, S79.leg1
  N97: LED80.anode, S77.leg1
  N98: LED81.anode, S78.leg1
  N99: LED82.anode, S81.leg1
  N100: LED83.anode, S82.leg1
  N101: LED84.cathode, S83.leg1
  N102: LED85.cathode, S84.leg1
  N103: LED86.cathode, S85.leg1
  N104: LED87.cathode, S86.leg1
  N105: LED88.cathode, S89.leg1
  N106: LED89.cathode, S90.leg1
  N107: LED90.cathode, S87.leg1
  N108: LED91.cathode, S88.leg1
  N109: LED92.cathode, S91.leg1
  N110: LED93.anode, S92.leg1
  N111: R11.Pin_0, S93.leg0, S94.leg0, S95.leg0, S96.leg0, S97.leg0, S98.leg0, S99.leg0, S100.leg0, S101.leg0, S102.leg0, LED104.anode, LED105.anode, LED106.anode, LED107.anode, LED108.anode, LED109.anode, LED110.anode, LED111.anode, LED112.anode, S173.leg0, LED178.anode, S174.leg0, S175.leg0, LED181.cathode, LED182.cathode, LED183.cathode
  N112: R11.Pin_1, Composant1.D2_PWM
  N113: LED94.anode, S93.leg1
  N114: LED95.anode, S94.leg1
  N115: LED96.anode, S95.leg1
  N116: LED97.anode, S99.leg1
  N117: LED98.anode, S98.leg1
  N118: LED99.anode, S96.leg1
  N119: LED100.anode, S97.leg1
  N120: LED101.anode, S100.leg1
  N121: LED102.anode, S101.leg1
  N122: LED103.anode, S102.leg1
  N123: LED104.cathode, S103.leg1
  N124: LED105.cathode, S104.leg1
  N125: LED106.cathode, S105.leg1
  N126: LED107.cathode, S106.leg1
  N127: LED108.cathode, S107.leg1
  N128: LED109.cathode, S110.leg1
  N129: LED110.cathode, S111.leg1
  N130: LED111.cathode, S108.leg1
  N131: LED112.cathode, S109.leg1
  N132: S112.leg1, LED178.cathode
  N133: R12.Pin_0, S113.leg0, S114.leg0, S115.leg0, S116.leg0, S117.leg0, S118.leg0, S119.leg0, S120.leg0, S121.leg0, S122.leg0, LED144.anode, LED145.anode, LED146.anode, LED147.anode, LED148.anode, LED149.anode, LED150.anode, LED151.anode, LED152.anode, LED173.anode, LED177.anode, S176.leg0, S177.leg0, LED184.cathode, LED185.cathode, S183.leg0
  N134: R12.Pin_1, Composant1.D31
  N135: LED114.anode, S113.leg1
  N136: LED115.anode, S114.leg1
  N137: LED116.anode, S115.leg1
  N138: LED117.anode, S116.leg1
  N139: LED118.anode, S120.leg1
  N140: LED119.anode, S119.leg1
  N141: LED120.anode, S117.leg1
  N142: LED121.anode, S118.leg1
  N143: LED122.anode, S121.leg1
  N144: LED123.anode, S122.leg1
  N145: R13.Pin_0, S123.leg0, S124.leg0, S125.leg0, S126.leg0, S127.leg0, S128.leg0, S129.leg0, S130.leg0, S131.leg0, S132.leg0, LED154.anode, LED155.anode, LED156.anode, LED157.anode, LED158.anode, LED159.anode, LED160.anode, LED161.anode, LED162.anode, LED175.anode, LED179.anode, LED180.anode, S179.leg0, S180.leg0, LED186.cathode, S184.leg0
  N146: R13.Pin_1, Composant1.D33
  N147: LED124.anode, S123.leg1
  N148: LED125.anode, S124.leg1
  N149: LED126.anode, S125.leg1
  N150: LED127.anode, S126.leg1
  N151: LED128.anode, S130.leg1
  N152: LED129.anode, S129.leg1
  N153: LED130.anode, S127.leg1
  N154: LED131.anode, S128.leg1
  N155: LED132.anode, S131.leg1
  N156: LED133.anode, S132.leg1
  N157: R14.Pin_0, S133.leg0, S134.leg0, S135.leg0, S136.leg0, S137.leg0, S138.leg0, S139.leg0, S140.leg0, S141.leg0, S142.leg0, LED164.anode, LED165.anode, LED166.anode, LED167.anode, LED168.anode, LED169.anode, LED170.anode, LED171.anode, LED172.anode, LED174.anode, LED176.anode, S178.leg0, S181.leg0, S182.leg0, LED187.anode, LED188.anode
  N158: R14.Pin_1, Composant1.D35
  N159: LED134.anode, S133.leg1
  N160: LED135.anode, S134.leg1
  N161: LED136.anode, S135.leg1
  N162: LED137.anode, S136.leg1
  N163: LED138.anode, S140.leg1
  N164: LED139.anode, S139.leg1
  N165: LED140.anode, S137.leg1
  N166: LED141.anode, S138.leg1
  N167: LED142.anode, S141.leg1
  N168: LED143.anode, S142.leg1
  N169: LED144.cathode, S143.leg1
  N170: LED145.cathode, S144.leg1
  N171: LED146.cathode, S145.leg1
  N172: LED147.cathode, S146.leg1
  N173: LED148.cathode, S147.leg1
  N174: LED149.cathode, S150.leg1
  N175: LED150.cathode, S151.leg1
  N176: LED151.cathode, S148.leg1
  N177: LED152.cathode, S149.leg1
  N178: S152.leg1, LED177.cathode
  N179: LED154.cathode, S153.leg1
  N180: LED155.cathode, S154.leg1
  N181: LED156.cathode, S155.leg1
  N182: LED157.cathode, S156.leg1
  N183: LED158.cathode, S157.leg1
  N184: LED159.cathode, S160.leg1
  N185: LED160.cathode, S161.leg1
  N186: LED161.cathode, S158.leg1
  N187: LED162.cathode, S159.leg1
  N188: S162.leg1, LED179.cathode
  N189: LED164.cathode, S163.leg1
  N190: LED165.cathode, S164.leg1
  N191: LED166.cathode, S165.leg1
  N192: LED167.cathode, S166.leg1
  N193: LED168.cathode, S167.leg1
  N194: LED169.cathode, S170.leg1
  N195: LED170.cathode, S171.leg1
  N196: LED171.cathode, S168.leg1
  N197: LED172.cathode, S169.leg1
  N198: S172.leg1, LED176.cathode
  N199: S173.leg1, LED173.cathode
  N200: LED174.cathode, S175.leg1
  N201: LED175.cathode, S174.leg1
  N202: LED180.cathode, S176.leg1
  N203: LED181.anode, S177.leg1
  N204: LED182.anode, S179.leg1
  N205: LED183.anode, S178.leg1
  N206: LED184.anode, S180.leg1
  N207: LED185.anode, S181.leg1
  N208: LED186.anode, S182.leg1
  N209: LED187.cathode, S183.leg1
  N210: LED188.cathode, S184.leg1
  N211: Composant1.GND, J3.GNDBREAK
  N212: Composant1.5V, R15.Pin_0
  VIN: Composant1.VIN, J3.GND, J3.PWR
  N213: Composant1.D1_TX0, R16.Pin_0
  N214: U2.MIDI_IN, R15.Pin_1
  N215: U2.MIDI_OUT, R16.Pin_1
